# Fritzing sketch chordtoy (saved by Fritzing 0.9.3b)
breadboards: 1

parts:
  Part1 = Arduino Uno (Rev3)
  R1 = Rotary Potentiometer (Small) [maximum_resistance=100kΩ package=THT]
  R2 = Rotary Potentiometer (Small) [maximum_resistance=100kΩ package=THT]
  R3 = Rotary Potentiometer (Small) [maximum_resistance=100kΩ package=THT]
  S1 = Toggle Switch [package=THT]
  R4 = Resistor [tolerance=±5% resistance=220 package=THT]
  R5 = Resistor [tolerance=±5% resistance=10k package=THT]
  LED1 = LED - 5mm [color="Red (633nm)" package="5 mm [THT]"]
  LED2 = LED - 5mm [color="Green (565nm)" package="5 mm [THT]"]
  R6 = Resistor [tolerance=±5% resistance=220 package=THT]
  DIN2 = DIN-5 jack (MIDI) [package=THT]
  R7 = Resistor [tolerance=±5% resistance=220 package=THT]
  DIN3 = DIN-5 jack (MIDI) [package=THT]
  R8 = Rotary Potentiometer (Small) [maximum_resistance=100kΩ package=THT]

nets:
  N1: Part1.A0, R8.wiper
  N2: Part1.A1, R2.wiper
  N3: Part1.A2, R3.wiper
  N4: Part1.A3, R1.wiper
  N5: Part1.D13/SCK, S1.COM, R5.Pin_1
  N6: Part1.D0/RX, DIN3.5
  N7: Part1.D1/TX, R7.Pin_1
  N8: Part1.D4, LED2.anode
  N9: Part1.D5_PWM, LED1.anode
  N10: Part1.GND, R1.leg1, R2.leg1, R3.leg1, R4.Pin_0, R5.Pin_0, R6.Pin_0, DIN2.2, DIN3.2, R8.leg1
  N11: Part1.VIN, R1.leg2, R2.leg2, R3.leg2, S1.L2, DIN2.4, R8.leg2
  N12: R4.Pin_1, LED1.cathode
  N13: LED2.cathode, R6.Pin_1
  N14: DIN2.5, R7.Pin_0

notes:
  KEY
  VAR
  INV
  RATE
  MAJOR
  MINOR
  MAJOR/MINOR SWITCH
  IN
  OUT
